// Logisim project RESPONSI_PENGURANGAN_WAHYUNI_PUTRA_223010503020.circ as structural Verilog: 3 circuits, main circuit main
module main (
  input  B_IN,
  input  [3:0] A,
  input  [3:0] B,
  output [3:0] R,
  output B_OUT
);

  wire FS_2_b_out, FS_3_b_out, FS_b_out, n7_segment_1_a_2, n7_segment_1_b_2, n7_segment_1_c_2,
       n7_segment_1_d_2, n7_segment_1_e, n7_segment_1_f, n7_segment_1_g, n7_segment_2_a_2, n7_segment_2_b_2,
       n7_segment_2_c_2, n7_segment_2_d_2, n7_segment_2_e, n7_segment_2_f, n7_segment_2_g, n7_segment_3_a_2,
       n7_segment_3_b_2, n7_segment_3_c_2, n7_segment_3_d_2, n7_segment_3_e, n7_segment_3_f, n7_segment_3_g;

  FULL_SUB FS (.B_IN(B_IN), .A(A[0]), .B(B[0]), .out_4(R[0]), .B_OUT(FS_b_out));
  _7_SEGMENT u_7_segment_1 (
    .A(A[3]), .B(A[2]), .C(A[1]), .D(A[0]), .a_2(n7_segment_1_a_2), .b_2(n7_segment_1_b_2),
    .c_2(n7_segment_1_c_2), .d_2(n7_segment_1_d_2), .e(n7_segment_1_e), .f(n7_segment_1_f), .g(n7_segment_1_g));
  _7_Segment_Display u_7_segment_display_1 (
    .g(n7_segment_1_g), .f(n7_segment_1_f), .a(n7_segment_1_a_2), .b(n7_segment_1_b_2), .e(n7_segment_1_e),
    .d(n7_segment_1_d_2), .c(n7_segment_1_c_2));  // open: dp
  FULL_SUB FS_2 (.B_IN(FS_b_out), .A(A[1]), .B(B[1]), .out_4(R[1]), .B_OUT(FS_2_b_out));
  _7_Segment_Display u_7_segment_display_2 (
    .g(n7_segment_2_g), .f(n7_segment_2_f), .a(n7_segment_2_a_2), .b(n7_segment_2_b_2), .e(n7_segment_2_e),
    .d(n7_segment_2_d_2), .c(n7_segment_2_c_2));  // open: dp
  FULL_SUB FS_3 (.B_IN(FS_2_b_out), .A(A[2]), .B(B[2]), .out_4(R[2]), .B_OUT(FS_3_b_out));
  _7_SEGMENT u_7_segment_2 (
    .A(B[3]), .B(B[2]), .C(B[1]), .D(B[0]), .a_2(n7_segment_2_a_2), .b_2(n7_segment_2_b_2),
    .c_2(n7_segment_2_c_2), .d_2(n7_segment_2_d_2), .e(n7_segment_2_e), .f(n7_segment_2_f), .g(n7_segment_2_g));
  FULL_SUB FS_4 (.B_IN(FS_3_b_out), .A(A[3]), .B(B[3]), .out_4(R[3]), .B_OUT(B_OUT));
  _7_SEGMENT u_7_segment_3 (
    .A(R[3]), .B(R[2]), .C(R[1]), .D(R[0]), .a_2(n7_segment_3_a_2), .b_2(n7_segment_3_b_2),
    .c_2(n7_segment_3_c_2), .d_2(n7_segment_3_d_2), .e(n7_segment_3_e), .f(n7_segment_3_f), .g(n7_segment_3_g));
  _7_Segment_Display u_7_segment_display_3 (
    .g(n7_segment_3_g), .f(n7_segment_3_f), .a(n7_segment_3_a_2), .b(n7_segment_3_b_2), .e(n7_segment_3_e),
    .d(n7_segment_3_d_2), .c(n7_segment_3_c_2), .dp(B_OUT));

  // Notes on the sheet:
  //   4 3 2 1
  //   4 3 2 1
  //   WAHYUNI PUTRA
  //   NIM 223010503020
  //   RESPONSI KELAS K SISTEM DIGITAL
  //   OPERASI PENGURANGAN
  //   -
  //   =
  //   4 3 2 1
endmodule

module FULL_SUB (
  input  B_IN,
  input  A,
  input  B,
  output out_4,
  output B_OUT
);

  wire and_1_out, and_2_out, not_1_out, not_2_out, xor_1_out;

  not not_1 (not_1_out, A);
  xor xor_1 (xor_1_out, A, B);
  and and_1 (and_1_out, B, not_1_out);
  not not_2 (not_2_out, xor_1_out);
  and and_2 (and_2_out, not_2_out, B_IN);
  xor xor_2 (out_4, B_IN, xor_1_out);
  or or_1 (B_OUT, and_2_out, and_1_out);
endmodule

module _7_SEGMENT (
  input  A,
  input  B,
  input  C,
  input  D,
  output a_2,
  output b_2,
  output c_2,
  output d_2,
  output e,
  output f,
  output g
);

  wire and_1_out, and_2_out, and_3_out, and_4_out, and_5_out, and_6_out, and_7_out, and_8_out, and_9_out,
       and_10_out, and_11_out, and_12_out, and_13_out, and_14_out, and_15_out, and_16_out, and_17_out,
       and_18_out, and_19_out, and_20_out, and_21_out, and_22_out, and_23_out, and_24_out, and_25_out,
       and_26_out, and_27_out, and_28_out, and_29_out, and_30_out, and_31_out, and_32_out, and_33_out,
       and_34_out, and_35_out, not_1_out, not_2_out, not_3_out, not_4_out, not_5_out, not_6_out, not_7_out,
       not_8_out, not_9_out, not_10_out, not_11_out, not_12_out, not_13_out, not_14_out, not_15_out,
       not_16_out, not_17_out, not_18_out, not_19_out, not_20_out, not_21_out, not_22_out, not_23_out,
       not_24_out, not_25_out, not_26_out, not_27_out, not_28_out, not_29_out, not_30_out, not_31_out,
       not_32_out, not_33_out, not_34_out, not_35_out, not_36_out, not_37_out, not_38_out, not_39_out,
       not_40_out, not_41_out, not_42_out, not_43_out;

  not not_1 (not_1_out, B);
  and and_1 (and_1_out, not_1_out, not_2_out);
  not not_2 (not_2_out, D);
  not not_3 (not_3_out, A);
  and and_2 (and_2_out, not_3_out, C);
  not not_4 (not_4_out, A);
  and and_3 (and_3_out, not_4_out, B, D);
  and and_4 (and_4_out, B, C);
  and and_5 (and_5_out, A, not_5_out, not_6_out);
  not not_5 (not_5_out, B);
  not not_6 (not_6_out, C);
  and and_6 (and_6_out, A, not_7_out);
  not not_7 (not_7_out, D);
  not not_8 (not_8_out, A);
  and and_7 (and_7_out, not_8_out, not_9_out);
  not not_9 (not_9_out, B);
  not not_10 (not_10_out, A);
  not not_11 (not_11_out, C);
  and and_8 (and_8_out, not_10_out, not_11_out, not_12_out);
  not not_12 (not_12_out, D);
  not not_13 (not_13_out, B);
  and and_9 (and_9_out, not_13_out, not_14_out);
  not not_14 (not_14_out, D);
  not not_15 (not_15_out, A);
  and and_10 (and_10_out, not_15_out, C, D);
  and and_11 (and_11_out, A, not_16_out, D);
  not not_16 (not_16_out, C);
  not not_17 (not_17_out, A);
  and and_12 (and_12_out, not_17_out, not_18_out);
  not not_18 (not_18_out, C);
  not not_19 (not_19_out, A);
  and and_13 (and_13_out, not_19_out, D);
  not not_20 (not_20_out, C);
  and and_14 (and_14_out, not_20_out, D);
  not not_21 (not_21_out, A);
  and and_15 (and_15_out, not_21_out, B);
  and and_16 (and_16_out, A, not_22_out);
  not not_22 (not_22_out, B);
  not not_23 (not_23_out, A);
  and and_17 (and_17_out, not_23_out, not_24_out, not_25_out);
  not not_24 (not_24_out, B);
  not not_25 (not_25_out, D);
  not not_26 (not_26_out, B);
  and and_18 (and_18_out, not_26_out, C, D);
  and and_19 (and_19_out, B, not_27_out, D);
  not not_27 (not_27_out, C);
  and and_20 (and_20_out, B, C, not_28_out);
  not not_28 (not_28_out, D);
  and and_21 (and_21_out, A, not_29_out);
  not not_29 (not_29_out, C);
  not not_30 (not_30_out, B);
  and and_22 (and_22_out, not_30_out, not_31_out);
  not not_31 (not_31_out, D);
  and and_23 (and_23_out, C, not_32_out);
  not not_32 (not_32_out, D);
  and and_24 (and_24_out, A, C);
  and and_25 (and_25_out, A, B);
  not not_33 (not_33_out, C);
  and and_26 (and_26_out, not_33_out, not_34_out);
  not not_34 (not_34_out, D);
  not not_35 (not_35_out, A);
  and and_27 (and_27_out, not_35_out, B, not_36_out);
  not not_36 (not_36_out, C);
  and and_28 (and_28_out, B, not_37_out);
  not not_37 (not_37_out, D);
  and and_29 (and_29_out, A, not_38_out);
  not not_38 (not_38_out, B);
  and and_30 (and_30_out, A, C);
  not not_39 (not_39_out, B);
  and and_31 (and_31_out, not_39_out, C);
  and and_32 (and_32_out, C, not_40_out);
  not not_40 (not_40_out, D);
  not not_41 (not_41_out, A);
  and and_33 (and_33_out, not_41_out, B, not_42_out);
  not not_42 (not_42_out, C);
  and and_34 (and_34_out, A, not_43_out);
  not not_43 (not_43_out, B);
  and and_35 (and_35_out, A, D);
  or or_1 (b_2, and_7_out, and_8_out, and_9_out, and_10_out, and_11_out);
  or or_2 (c_2, and_12_out, and_13_out, and_14_out, and_15_out, and_16_out);
  or or_3 (d_2, and_17_out, and_18_out, and_19_out, and_20_out, and_21_out);
  or or_4 (e, and_22_out, and_23_out, and_24_out, and_25_out);
  or or_5 (f, and_26_out, and_27_out, and_28_out, and_29_out, and_30_out);
  or or_6 (g, and_31_out, and_32_out, and_33_out, and_34_out, and_35_out);
  or or_7 (a_2, and_1_out, and_2_out, and_3_out, and_4_out, and_5_out, and_6_out);
endmodule
