// Logisim project FULL ADDER 4 BIT.circ as structural Verilog: 2 circuits, main circuit main
// FA
module main (
  input  in_1,
  input  in_2,
  input  in_3,
  output out_4,
  output out_5
);

  wire and_1_out, and_2_out, xor_1_out;

  xor xor_1 (xor_1_out, in_2, in_3);
  and and_1 (and_1_out, in_2, in_3);
  xor xor_2 (out_4, in_1, xor_1_out);
  and and_2 (and_2_out, in_1, xor_1_out);
  or or_1 (out_5, and_2_out, and_1_out);
endmodule

module FULL_ADDER (
  input  C0,
  input  B1,
  input  A1,
  input  B2,
  input  A2,
  input  B3,
  input  A3,
  input  B4,
  input  A4,
  output C4,
  output S1,
  output S2,
  output S3,
  output S4
);

  wire main_1_out_4, main_2_out_4, main_3_out_4;

  main main_1 (.in_1(A1), .in_2(B1), .in_3(C0), .out_4(main_1_out_4), .out_5(S1));
  main main_2 (.in_1(A2), .in_2(B2), .in_3(main_1_out_4), .out_4(main_2_out_4), .out_5(S2));
  main main_3 (.in_1(A3), .in_2(B3), .in_3(main_2_out_4), .out_4(main_3_out_4), .out_5(S3));
  main main_4 (.in_1(A4), .in_2(B4), .in_3(main_3_out_4), .out_4(C4), .out_5(S4));

  // Notes on the sheet:
  //   CI
endmodule
