// Logisim project 4-BIT KIWKIW.circ as structural Verilog: 1 circuit, main circuit main
module main (
  input  in_1,
  input  [3:0] A,
  input  [3:0] B,
  output [3:0] S,
  output out_5
);

  Adder #(.width(4)) adder_1 (.a(A), .b(B), .out(S), .cin(in_1), .cout(out_5));

  // Notes on the sheet:
  //   4 3 2 1 
  //   4 3 2 1 
  //   4 3 2 1 
endmodule
