// Logisim project PARALER ADDER.circ as structural Verilog: 2 circuits, main circuit main
module main (
  input  C_IN,
  input  A,
  input  B,
  output SUM,
  output C_OUT
);

  wire and_1_out, and_2_out, xor_1_out;

  xor xor_1 (xor_1_out, A, B);
  xor xor_2 (SUM, xor_1_out, C_IN);
  and and_1 (and_1_out, C_IN, xor_1_out);
  and and_2 (and_2_out, B, A);
  or or_1 (C_OUT, and_1_out, and_2_out);
endmodule

// S1
module FA (
  input  B1_A1_CI,
  input  in_2,
  input  in_3,
  input  A2_B2,
  input  in_5,
  input  A3_B3,
  input  in_7,
  input  A4_B4,
  input  in_9,
  output S1,
  output S2,
  output S3,
  output S4,
  output C4
);

  wire main_1_c_out, main_2_c_out, main_3_c_out;

  main main_1 (.C_IN(in_3), .A(in_2), .B(B1_A1_CI), .SUM(S1), .C_OUT(main_1_c_out));
  main main_2 (.C_IN(main_1_c_out), .A(A2_B2), .B(in_5), .SUM(S2), .C_OUT(main_2_c_out));
  main main_3 (.C_IN(main_2_c_out), .A(A3_B3), .B(in_7), .SUM(S3), .C_OUT(main_3_c_out));
  main main_4 (.C_IN(main_3_c_out), .A(A4_B4), .B(in_9), .SUM(S4), .C_OUT(C4));
endmodule
