// Logisim project CLOCK SRFF.circ as structural Verilog: 1 circuit, main circuit main
module main (
  input  S,
  input  R,
  output Q,
  output Q_2
);

  wire clock_1_out, nand_1_out, nand_2_out;

  Clock clock_1 (.out(clock_1_out));
  nand nand_1 (nand_1_out, S, clock_1_out);
  nand nand_2 (nand_2_out, clock_1_out, R);
  nor nor_1 (Q, nand_1_out, Q_2);
  nor nor_2 (Q_2, Q, nand_2_out);
endmodule
