// Logisim project JK REAL.circ as structural Verilog: 1 circuit, main circuit main
module main (
  input  J,
  input  K,
  input  SET,
  input  RESET,
  output LED_1,
  output LED_2
);

  wire CL_out;

  Clock CL (.out(CL_out));
  J_K_Flip_Flop j_k_ff_1 (.J(J), .clk(CL_out), .K(K), .Q(LED_1), .Qn(LED_2), .preset(SET), .reset(RESET));  // open: en
endmodule
