// Logisim project NOR.circ as structural Verilog: 1 circuit, main circuit main
module main (
  input  S,
  input  S_2,
  input  R,
  input  R_2,
  input  S_3,
  input  S_4,
  input  R_3,
  input  R_4,
  output Q,
  output Q_prime,
  output Q_prime_2,
  output Q_2,
  output Q_3,
  output Q_prime_3,
  output Q_4,
  output Q_5
);

  nor nor_1 (Q, S, Q_prime_2);
  nor nor_2 (Q_prime_2, Q, R);
  nor nor_3 (Q_3, S_3, Q_4);
  nor nor_4 (Q_4, Q_3, R_3);
  nor nor_5 (Q_prime, S_2, Q_2);
  nor nor_6 (Q_2, Q_prime, R_2);
  nor nor_7 (Q_prime_3, S_4, Q_5);
  nor nor_8 (Q_5, Q_prime_3, R_4);
endmodule
