// Logisim project SRFF.circ as structural Verilog: 1 circuit, main circuit main
module main (
  input  S,
  input  S_2,
  input  R,
  input  R_2,
  input  S_3,
  input  S_4,
  input  R_3,
  input  R_4,
  output Q,
  output Q_2,
  output Q_prime,
  output Q_prime_2,
  output Q_3,
  output Q_4,
  output Q_prime_3,
  output Q_prime_4
);

  nand nand_1 (Q, S, Q_prime);
  nand nand_2 (Q_prime, Q, R);
  nand nand_3 (Q_3, S_3, Q_prime_3);
  nand nand_4 (Q_prime_3, Q_3, R_3);
  nand nand_5 (Q_2, S_2, Q_prime_2);
  nand nand_6 (Q_prime_2, Q_2, R_2);
  nand nand_7 (Q_4, S_4, Q_prime_4);
  nand nand_8 (Q_prime_4, Q_4, R_4);
endmodule
